// Logisim project ceepoo.circ as structural Verilog: 13 circuits, main circuit registre
module bboard (
  input  [7:0] in_1,
  input  [1:0] in_2,
  input  str,
  input  ld,
  input  ena,
  input  set,
  input  _0,
  input  [2:0] regsel,
  input  wipe,
  input  _8sa,
  input  _16sa,
  input  tmpset,
  input  OP,
  input  acc1sel,
  input  [2:0] in_15,
  input  [1:0] in_16,
  input  [1:0] in_17
);

  wire undriven;
  wire [1:0] demultiplexer_1_out0, demultiplexer_1_out1, demultiplexer_1_out2, demultiplexer_1_out3,
       demultiplexer_1_out4, demultiplexer_1_out5, demultiplexer_1_out6, demultiplexer_1_out7;
  wire [7:0] _8_MAR_q, alu_1_acc1, alu_1_acc_0, bus1_1_buso, IR_q, register_1_q, registre_1_o,
       registre_1_out_4, registre_2_out_4, registre_3_out_4, registre_4_out_4, registre_5_out_4,
       registre_6_out_4, registre_7_out_4, registre_8_out_4, registre_9_out_4, registre_10_out_4,
       registre_11_out_4;
  wire [15:0] n16registre_1_out_4, register_2_q;

  // Probe on in_1
  registre registre_1 (.I(in_1), .s_e(in_2), .O(registre_1_o), .out_4(registre_1_out_4));  // open: in_2
  // Probe on registre_1_out_4
  Demultiplexer #(.select(3), .width(2)) demultiplexer_1 (
    .out0(demultiplexer_1_out0), .out1(demultiplexer_1_out1), .out2(demultiplexer_1_out2),
    .out3(demultiplexer_1_out3), .out4(demultiplexer_1_out4), .out5(demultiplexer_1_out5),
    .out6(demultiplexer_1_out6), .out7(demultiplexer_1_out7), .in({set, ena}), .sel(regsel));  // open: en
  registre registre_2 (
    .I(registre_1_o), .s_e(demultiplexer_1_out2), .O(registre_1_o), .out_4(registre_2_out_4), .in_2(wipe));
  registre registre_3 (
    .I(registre_1_o), .s_e(demultiplexer_1_out1), .O(registre_1_o), .out_4(registre_3_out_4), .in_2(wipe));
  registre registre_4 (
    .I(registre_1_o), .s_e(demultiplexer_1_out0), .O(registre_1_o), .out_4(registre_4_out_4), .in_2(wipe));
  // Probe on registre_3_out_4
  // Probe on registre_4_out_4
  // Probe on registre_2_out_4
  _16registre u_16registre_1 (.out_4(n16registre_1_out_4));  // open: I, s_e, O, in_2
  // Probe on n16registre_1_out_4
  Register IR (.D(registre_1_o), .Q(IR_q), .clk(undriven));  // open: en, clr
  registre registre_5 (
    .I(registre_1_o), .s_e(demultiplexer_1_out3), .O(registre_1_o), .out_4(registre_5_out_4), .in_2(wipe));
  registre registre_6 (
    .I(registre_1_o), .s_e(demultiplexer_1_out4), .O(registre_1_o), .out_4(registre_6_out_4), .in_2(wipe));
  registre registre_7 (
    .I(registre_1_o), .s_e(demultiplexer_1_out5), .O(registre_1_o), .out_4(registre_7_out_4), .in_2(wipe));
  // Probe on registre_7_out_4
  // Probe on registre_6_out_4
  // Probe on registre_5_out_4
  registre registre_8 (
    .I(registre_1_o), .s_e(demultiplexer_1_out7), .O(registre_1_o), .out_4(registre_8_out_4), .in_2(wipe));
  registre registre_9 (
    .I(registre_1_o), .s_e(demultiplexer_1_out6), .O(registre_1_o), .out_4(registre_9_out_4), .in_2(wipe));
  // Probe on registre_9_out_4
  // Probe on registre_8_out_4
  ccircuitwrapper ccircuitwrapper_1 ();  // open: SET_8_MAR, SET_16_MAR, SET_RAM, SET_TMP, BUS_1, IAR0, IAR1, SET_ALU_ACC1, SET_IR, IN_FBUFFLAG, EN_RAM, SET_OP, ACC1, ACC0, IR, RS_E, RSEL
  Register _8_MAR (.D(registre_1_o), .Q(_8_MAR_q), .clk(_8sa));  // open: en, clr
  // Probe on registre_1_o
  // Probe on registre_1_o
  // Probe on registre_1_o
  // Probe on registre_1_o
  // Probe on {registre_1_o, _8_MAR_q}
  Register register_1 (.D(registre_1_o), .Q(register_1_q), .clk(tmpset));  // open: en, clr
  ALU alu_1 (
    .op(in_15), .acc_0(alu_1_acc_0), .a(registre_1_o), .b(bus1_1_buso), .acc1(alu_1_acc1), .acc1sel(acc1sel));  // open: cin, zero, cout, a_larger, eq, FULL
  registre registre_10 (.I(alu_1_acc1), .s_e(in_16), .O(registre_1_o), .out_4(registre_10_out_4));  // open: in_2
  // Probe on registre_10_out_4
  Register #(.width(16)) register_2 (
    .D({registre_1_o, _8_MAR_q}), .Q(register_2_q), .clk(_16sa), .clr(_0));  // open: en
  bus1 bus1_1 (.OP(OP), .BUSI(register_1_q), .BUSO(bus1_1_buso));
  // Probe on bus1_1_buso
  registre registre_11 (.I(alu_1_acc_0), .s_e(in_17), .O(registre_1_o), .out_4(registre_11_out_4));  // open: in_2
  // Probe on registre_11_out_4
  RAM #(.addrWidth(16)) ram_1 (.addr(register_2_q), .data(registre_1_o), .clk(str), .ld(ld));  // open: sel, clr
endmodule

module registre (
  input  [7:0] I,
  input  in_2,
  input  [1:0] s_e,
  output [7:0] out_4,
  output [7:0] O
);

  Register register_1 (.D(I), .Q(out_4), .clk(s_e[1]), .clr(in_2));  // open: en
  assign O = s_e[0] ? out_4 : 8'bz;  // Controlled_Buffer controlled_buffer_1
  Pull_Resistor pull_resistor_1 (.node(s_e[0]));
endmodule

module ALU (
  input  [7:0] a,
  input  [7:0] b,
  input  cin,
  input  acc1sel,
  input  [2:0] op,
  output zero,
  output [7:0] acc_0,
  output [7:0] acc1,
  output cout,
  output FULL,
  output a_larger,
  output eq
);

  wire adder_1_cout, decoder_1_out0, decoder_1_out1, decoder_1_out2, decoder_1_out3, decoder_1_out4,
       decoder_1_out5, decoder_1_out6, not_2_out, or_2_out, sh_l_1_cout, sh_r_1_cout;
  wire [7:0] adder_1_out, and_1_out, buffer_1_out, controlled_buffer_1_out, not_1_out, or_1_out,
       pull_resistor_2_node, sh_l_1_out_3, sh_r_1_out_4, xor_1_out;

  assign not_1_out = ~a;  // NOT_Gate not_1, 8 bits wide
  Comparator #(.mode("unsigned")) comparator_1 (.a(a), .b(b), .gt(a_larger), .eq(eq));  // open: lt
  assign xor_1_out = a ^ b;  // XOR_Gate xor_1, 8 bits wide
  assign or_1_out = a | b;  // OR_Gate or_1, 8 bits wide
  assign and_1_out = a & b;  // AND_Gate and_1, 8 bits wide
  sh_l sh_l_1 (.in_2(a), .out_3(sh_l_1_out_3), .cin(cin), .cout(sh_l_1_cout));
  assign controlled_buffer_1_out = decoder_1_out2 ? sh_l_1_out_3 : 8'bz;  // Controlled_Buffer controlled_buffer_1
  assign cout = decoder_1_out2 ? sh_l_1_cout : 1'bz;  // Controlled_Buffer controlled_buffer_2
  assign cout = decoder_1_out1 ? sh_r_1_cout : 1'bz;  // Controlled_Buffer controlled_buffer_3
  sh_r sh_r_1 (.in_1(a), .out_4(sh_r_1_out_4), .cout(sh_r_1_cout), .cin(cin));
  assign controlled_buffer_1_out = decoder_1_out1 ? sh_r_1_out_4 : 8'bz;  // Controlled_Buffer controlled_buffer_4
  Adder adder_1 (.a(a), .b(b), .out(adder_1_out), .cin(cin), .cout(adder_1_cout));
  assign controlled_buffer_1_out = decoder_1_out0 ? adder_1_out : 8'bz;  // Controlled_Buffer controlled_buffer_5
  assign cout = decoder_1_out0 ? adder_1_cout : 1'bz;  // Controlled_Buffer controlled_buffer_6
  Decoder #(.select(3)) decoder_1 (
    .out0(decoder_1_out0), .out1(decoder_1_out1), .out2(decoder_1_out2), .out3(decoder_1_out3),
    .out4(decoder_1_out4), .out5(decoder_1_out5), .out6(decoder_1_out6), .sel(op));  // open: out7, en
  assign controlled_buffer_1_out = decoder_1_out6 ? xor_1_out : 8'bz;  // Controlled_Buffer controlled_buffer_7
  assign controlled_buffer_1_out = decoder_1_out5 ? or_1_out : 8'bz;  // Controlled_Buffer controlled_buffer_8
  assign controlled_buffer_1_out = decoder_1_out4 ? and_1_out : 8'bz;  // Controlled_Buffer controlled_buffer_9
  assign controlled_buffer_1_out = decoder_1_out3 ? not_1_out : 8'bz;  // Controlled_Buffer controlled_buffer_10
  assign buffer_1_out = controlled_buffer_1_out;  // Buffer buffer_1, 8 bits wide
  Pull_Resistor pull_resistor_1 (.node(buffer_1_out));
  assign acc_0 = not_2_out ? controlled_buffer_1_out : 8'bz;  // Controlled_Buffer controlled_buffer_11
  not not_2 (not_2_out, acc1sel);
  assign acc1 = acc1sel ? controlled_buffer_1_out : 8'bz;  // Controlled_Buffer controlled_buffer_12
  or or_2 (or_2_out, buffer_1_out[0], buffer_1_out[1], buffer_1_out[2], buffer_1_out[3], buffer_1_out[4], buffer_1_out[5], buffer_1_out[6], buffer_1_out[7]);
  not not_3 (zero, or_2_out);
  Pull_Resistor pull_resistor_2 (.node(pull_resistor_2_node));
  assign pull_resistor_2_node = controlled_buffer_1_out;  // Buffer buffer_2, 8 bits wide
  and and_2 (FULL, pull_resistor_2_node[0], pull_resistor_2_node[1], pull_resistor_2_node[2], pull_resistor_2_node[3], pull_resistor_2_node[4], pull_resistor_2_node[5], pull_resistor_2_node[6], pull_resistor_2_node[7]);
endmodule

module sh_l (
  input  cin,
  input  [7:0] in_2,
  output [7:0] out_3,
  output cout
);


  assign cout = in_2[7];
  assign out_3 = {in_2[6:0], cin};
endmodule

module sh_r (
  input  [7:0] in_1,
  input  cin,
  output cout,
  output [7:0] out_4
);


  assign cout = in_1[0];
  assign out_4 = {cin, in_1[7:1]};
endmodule

module clock (
  input  in_1,
  output clk,
  output clk_e,
  output clk_s
);

  wire counter_2_q, not_1_out;

  Counter #(.width(1), .max('h1)) counter_1 (.Q(clk), .clk(in_1));  // open: load, D, count, carry, clr
  Counter #(.width(1), .max('h1)) counter_2 (.Q(counter_2_q), .clk(not_1_out));  // open: load, D, count, carry, clr
  not not_1 (not_1_out, in_1);
  or or_1 (clk_e, clk, counter_2_q);
  and and_1 (clk_s, clk, counter_2_q);
endmodule

module stepper (
  input  clk,
  input  rst,
  output _1,
  output _2,
  output _3,
  output _4,
  output _5,
  output _6,
  output _0
);

  wire d_ff_1_q, d_ff_2_q, d_ff_3_q, d_ff_4_q, d_ff_5_q, not_1_out, not_2_out, not_3_out, not_4_out,
       not_5_out, not_6_out, not_7_out;

  or or_1 (_0, rst, not_1_out);
  not not_1 (not_1_out, d_ff_1_q);
  not not_2 (not_2_out, rst);
  and and_1 (_1, d_ff_1_q, not_4_out);
  D_Flip_Flop d_ff_1 (.clk(clk), .D(not_2_out), .Q(d_ff_1_q), .reset(rst));  // open: Qn, preset, en
  and and_2 (_2, d_ff_2_q, not_3_out);
  not not_3 (not_3_out, d_ff_4_q);
  not not_4 (not_4_out, d_ff_2_q);
  D_Flip_Flop d_ff_2 (.clk(clk), .D(d_ff_1_q), .Q(d_ff_2_q), .reset(rst));  // open: Qn, preset, en
  and and_3 (_3, d_ff_4_q, not_5_out);
  not not_5 (not_5_out, d_ff_3_q);
  D_Flip_Flop d_ff_3 (.clk(clk), .D(d_ff_4_q), .Q(d_ff_3_q), .reset(rst));  // open: Qn, preset, en
  D_Flip_Flop d_ff_4 (.clk(clk), .D(d_ff_2_q), .Q(d_ff_4_q), .reset(rst));  // open: Qn, preset, en
  and and_4 (_4, d_ff_3_q, not_6_out);
  not not_6 (not_6_out, d_ff_5_q);
  D_Flip_Flop d_ff_5 (.clk(clk), .D(d_ff_3_q), .Q(d_ff_5_q), .reset(rst));  // open: Qn, preset, en
  and and_5 (_5, d_ff_5_q, not_7_out);
  not not_7 (not_7_out, _6);
  D_Flip_Flop d_ff_6 (.clk(clk), .D(d_ff_5_q), .Q(_6), .reset(rst));  // open: Qn, preset, en
endmodule

module control_circuit (
  input  [7:0] IR,
  input  fullbuffflag,
  output _8MAR,
  output RAM,
  output _16MAR,
  output ACC1,
  output ACC1_2,
  output ACC0,
  output ACC0_2,
  output [2:0] OP,
  output RSET,
  output RAM_2,
  output IAR0,
  output TMP,
  output [2:0] RSEL,
  output IAR1,
  output REN,
  output bus1,
  output IR_2,
  output IAR0_2,
  output IAR1_2,
  output acc1sel
);

  wire and_8_out, and_9_out, and_10_out, and_11_out, and_12_out, and_24_out, and_25_out, clock_1_clk,
       clock_1_clk_e, clock_1_clk_s, clock_2_out, d_ff_1_q, or_1_out, or_2_out, or_3_out, or_4_out, or_5_out,
       or_6_out, or_7_out, or_8_out, or_9_out, or_10_out, or_11_out, or_12_out, or_13_out, or_14_out,
       or_15_out, or_16_out, or_17_out, or_18_out, or_19_out, stepper8_1__0, stepper8_1__1, stepper8_1__2,
       stepper8_1__3, stepper8_1__4, stepper8_1__5, stepper8_1__6, stepper8_1__7, stepper8_1__8;

  clock clock_1 (.in_1(clock_2_out), .clk(clock_1_clk), .clk_e(clock_1_clk_e), .clk_s(clock_1_clk_s));
  Clock clock_2 (.out(clock_2_out));
  and and_1 (RAM, clock_1_clk_e, or_1_out);
  and and_2 (ACC1, clock_1_clk_e, or_2_out);
  and and_3 (ACC0, clock_1_clk_e, or_3_out);
  and and_4 (RSET, clock_1_clk_e, or_4_out);
  and and_5 (IAR0, clock_1_clk_e, or_5_out);
  and and_6 (IAR1, clock_1_clk_e, or_6_out);
  and and_7 (bus1, clock_1_clk_e, or_7_out);
  buf or_1 (or_1_out, stepper8_1__2);  // OR_Gate
  and and_8 (and_8_out, stepper8_1__4, d_ff_1_q);
  buf or_2 (or_2_out, and_8_out);  // OR_Gate
  buf or_3 (or_3_out, stepper8_1__3);  // OR_Gate
  // OR_Gate or_4 has open pins: out=or_4_out
  buf or_5 (or_5_out, stepper8_1__0);  // OR_Gate
  buf or_6 (or_6_out, stepper8_1__1);  // OR_Gate
  or or_7 (or_7_out, stepper8_1__0, and_9_out);
  and and_9 (and_9_out, stepper8_1__1, d_ff_1_q);
  stepper8 stepper8_1 (
    .clk(clock_1_clk), .rst(stepper8_1__8), ._0(stepper8_1__0), ._1(stepper8_1__1), ._2(stepper8_1__2),
    ._3(stepper8_1__3), ._4(stepper8_1__4), ._5(stepper8_1__5), ._6(stepper8_1__6), ._7(stepper8_1__7),
    ._8(stepper8_1__8));
  buf or_8 (or_8_out, stepper8_1__0);  // OR_Gate
  buf or_9 (or_9_out, stepper8_1__1);  // OR_Gate
  and and_10 (and_10_out, stepper8_1__1, d_ff_1_q);
  buf or_10 (or_10_out, and_10_out);  // OR_Gate
  buf or_11 (or_11_out, stepper8_1__0);  // OR_Gate
  // OR_Gate or_12 has open pins: out=or_12_out
  // OR_Gate or_13 has open pins: out=or_13_out
  // OR_Gate or_14 has open pins: out=or_14_out
  buf or_15 (or_15_out, stepper8_1__2);  // OR_Gate
  buf or_16 (or_16_out, stepper8_1__3);  // OR_Gate
  and and_11 (and_11_out, stepper8_1__4, d_ff_1_q);
  buf or_17 (or_17_out, and_11_out);  // OR_Gate
  and and_12 (and_12_out, stepper8_1__1, d_ff_1_q);
  buf or_18 (or_18_out, and_12_out);  // OR_Gate
  buf or_19 (or_19_out, stepper8_1__0);  // OR_Gate
  and and_13 (_8MAR, clock_1_clk_s, or_8_out);
  and and_14 (_16MAR, clock_1_clk_s, or_9_out);
  and and_15 (ACC1_2, clock_1_clk_s, or_10_out);
  and and_16 (ACC0_2, clock_1_clk_s, or_11_out);
  and and_17 (RAM_2, clock_1_clk_s, or_12_out);
  and and_18 (TMP, clock_1_clk_s, or_13_out);
  and and_19 (REN, clock_1_clk_s, or_14_out);
  and and_20 (IR_2, clock_1_clk_s, or_15_out);
  and and_21 (IAR0_2, clock_1_clk_s, or_16_out);
  and and_22 (IAR1_2, clock_1_clk_s, or_17_out);
  and and_23 (acc1sel, clock_1_clk_s, or_18_out);
  D_Flip_Flop d_ff_1 (.clk(and_24_out), .D(fullbuffflag), .Q(d_ff_1_q), .reset(and_25_out));  // open: Qn, preset, en
  and and_24 (and_24_out, clock_1_clk_s, or_19_out);
  and and_25 (and_25_out, clock_1_clk_s, stepper8_1__4);

  // Notes on the sheet:
  //   ENABLES
  //   SETS
endmodule

module bus1 (
  input  [7:0] BUSI,
  input  OP,
  output [7:0] BUSO
);

  wire not_1_out;

  and and_1 (BUSO[7], BUSI[7], not_1_out);
  and and_2 (BUSO[6], BUSI[6], not_1_out);
  and and_3 (BUSO[5], BUSI[5], not_1_out);
  and and_4 (BUSO[4], BUSI[4], not_1_out);
  and and_5 (BUSO[2], BUSI[2], not_1_out);
  and and_6 (BUSO[1], BUSI[1], not_1_out);
  and and_7 (BUSO[3], BUSI[3], not_1_out);
  not not_1 (not_1_out, OP);
  or or_1 (BUSO[0], BUSI[0], OP);
endmodule

module stepper8 (
  input  clk,
  input  rst,
  output _1,
  output _2,
  output _3,
  output _4,
  output _5,
  output _0,
  output _6,
  output _7,
  output _8
);

  wire d_ff_1_q, d_ff_2_q, d_ff_3_q, d_ff_4_q, d_ff_5_q, d_ff_6_q, d_ff_7_q, not_1_out, not_2_out, not_3_out,
       not_4_out, not_5_out, not_6_out, not_7_out, not_8_out, not_9_out;

  or or_1 (_0, rst, not_1_out);
  not not_1 (not_1_out, d_ff_1_q);
  not not_2 (not_2_out, rst);
  and and_1 (_1, d_ff_1_q, not_3_out);
  D_Flip_Flop d_ff_1 (.clk(clk), .D(not_2_out), .Q(d_ff_1_q), .reset(rst));  // open: Qn, preset, en
  and and_2 (_2, d_ff_2_q, not_4_out);
  not not_3 (not_3_out, d_ff_2_q);
  not not_4 (not_4_out, d_ff_3_q);
  D_Flip_Flop d_ff_2 (.clk(clk), .D(d_ff_1_q), .Q(d_ff_2_q), .reset(rst));  // open: Qn, preset, en
  and and_3 (_3, d_ff_3_q, not_5_out);
  not not_5 (not_5_out, d_ff_4_q);
  D_Flip_Flop d_ff_3 (.clk(clk), .D(d_ff_2_q), .Q(d_ff_3_q), .reset(rst));  // open: Qn, preset, en
  D_Flip_Flop d_ff_4 (.clk(clk), .D(d_ff_3_q), .Q(d_ff_4_q), .reset(rst));  // open: Qn, preset, en
  and and_4 (_4, d_ff_4_q, not_6_out);
  not not_6 (not_6_out, d_ff_5_q);
  D_Flip_Flop d_ff_5 (.clk(clk), .D(d_ff_4_q), .Q(d_ff_5_q), .reset(rst));  // open: Qn, preset, en
  and and_5 (_5, d_ff_5_q, not_7_out);
  not not_7 (not_7_out, d_ff_6_q);
  D_Flip_Flop d_ff_6 (.clk(clk), .D(d_ff_5_q), .Q(d_ff_6_q), .reset(rst));  // open: Qn, preset, en
  and and_6 (_6, d_ff_6_q, not_8_out);
  not not_8 (not_8_out, d_ff_7_q);
  D_Flip_Flop d_ff_7 (.clk(clk), .D(d_ff_6_q), .Q(d_ff_7_q), .reset(rst));  // open: Qn, preset, en
  and and_7 (_7, d_ff_7_q, not_9_out);
  not not_9 (not_9_out, _8);
  D_Flip_Flop d_ff_8 (.clk(clk), .D(d_ff_7_q), .Q(_8), .reset(rst));  // open: Qn, preset, en
endmodule

module ccircuitwrapper (
  input  IN_FBUFFLAG,
  input  [7:0] IR,
  output [1:0] ACC1,
  output [1:0] ACC0,
  output SET_8_MAR,
  output SET_16_MAR,
  output SET_RAM,
  output SET_TMP,
  output [1:0] RS_E,
  output [2:0] RSEL,
  output BUS_1,
  output [1:0] IAR0,
  output [1:0] IAR1,
  output SET_ALU_ACC1,
  output SET_IR,
  output EN_RAM,
  output [2:0] SET_OP
);

  control_circuit control_circuit_1 (
    .RAM(EN_RAM), .ACC0(ACC0[0]), .RSET(RS_E[0]), .OP(SET_OP), ._8MAR(SET_8_MAR), ._16MAR(SET_16_MAR),
    .RAM_2(SET_RAM), .TMP(SET_TMP), .IR_2(SET_IR), .IAR0_2(IAR0[1]), .IAR1_2(IAR1[0]), .IAR0(IAR0[0]),
    .IAR1(IAR1[1]), .ACC1(ACC1[0]), .ACC1_2(ACC1[1]), .ACC0_2(ACC0[1]), .acc1sel(SET_ALU_ACC1),
    .fullbuffflag(IN_FBUFFLAG), .bus1(BUS_1), .REN(RS_E[1]), .RSEL(RSEL));  // open: IR
endmodule

module _16_mem_test (
  input  [15:0] in_1,
  input  in_2,
  input  in_3,
  input  in_4,
  input  in_5
);

  wire and_1_out, and_2_out, and_3_out, and_4_out, and_5_out, clock_1_out, clock_2_clk, clock_2_clk_e,
       clock_2_clk_s, or_1_out, or_2_out, stepper_1__0, stepper_1__1, stepper_1__2, stepper_1__3,
       stepper_1__6;
  wire [7:0] controlled_buffer_1_out, shift_register_1_out, shift_register_2_q0, shift_register_2_q1,
       shift_register_3_out, shift_register_4_q0, shift_register_4_q1;
  wire [15:0] controlled_buffer_2_out, register_1_q, register_2_q;

  Clock clock_1 (.out(clock_1_out));
  clock clock_2 (.in_1(clock_1_out), .clk(clock_2_clk), .clk_e(clock_2_clk_e), .clk_s(clock_2_clk_s));
  Register #(.width(16)) register_1 (.D(in_1), .Q(register_1_q), .clk(in_2));  // open: en, clr
  Shift_Register #(.width(8), .length(2)) shift_register_1 (
    .clk(in_4), .out(shift_register_1_out), .load(in_3), .d0(register_1_q[15:8]), .d1(register_1_q[7:0]));  // open: shift, in, clr, q0, q1
  // Probe on register_1_q[15:8]
  // Probe on register_1_q[7:0]
  stepper stepper_1 (
    .clk(clock_2_clk), .rst(stepper_1__6), ._0(stepper_1__0), ._1(stepper_1__1), ._2(stepper_1__2),
    ._3(stepper_1__3), ._6(stepper_1__6));  // open: _4, _5
  and and_1 (and_1_out, clock_2_clk_e, stepper_1__0);
  and and_2 (and_2_out, clock_2_clk_s, or_1_out);
  or or_1 (or_1_out, stepper_1__1, stepper_1__0, stepper_1__2);
  Shift_Register #(.width(8), .length(2)) shift_register_2 (
    .in(shift_register_1_out), .clk(in_4), .q0(shift_register_2_q0), .q1(shift_register_2_q1));  // open: shift, out, load, clr, d0, d1
  Register #(.width(16)) register_2 (.Q(register_2_q));  // open: D, en, clk, clr
  and and_3 (and_3_out, clock_2_clk_e, or_2_out);
  or or_2 (or_2_out, stepper_1__1, stepper_1__2);
  and and_4 (and_4_out, clock_2_clk_e, stepper_1__3);
  and and_5 (and_5_out, clock_2_clk_s, stepper_1__3);
  // Probe on shift_register_2_q1
  // Probe on shift_register_2_q0
  assign controlled_buffer_1_out = and_3_out ? shift_register_3_out : 8'bz;  // Controlled_Buffer controlled_buffer_1
  Shift_Register #(.width(8), .length(2)) shift_register_3 (
    .clk(and_2_out), .out(shift_register_3_out), .load(and_1_out), .d0(register_2_q[15:8]),
    .d1(register_2_q[7:0]));  // open: shift, in, clr, q0, q1
  Register #(.width(16)) register_3 (.D({shift_register_2_q0, shift_register_2_q1}), .clk(in_5));  // open: en, Q, clr
  // Probe on register_2_q[15:8]
  // Probe on register_2_q[7:0]
  // Probe on controlled_buffer_1_out
  Shift_Register #(.width(8), .length(2)) shift_register_4 (
    .in(controlled_buffer_1_out), .clk(and_2_out), .q0(shift_register_4_q0), .q1(shift_register_4_q1));  // open: shift, out, load, clr, d0, d1
  // Probe on shift_register_4_q0
  // Probe on shift_register_4_q1
  assign controlled_buffer_2_out = and_4_out ? {shift_register_4_q0, shift_register_4_q1} : 16'bz;  // Controlled_Buffer controlled_buffer_2
  Register #(.width(16)) register_4 (.D(controlled_buffer_2_out), .clk(and_5_out));  // open: en, Q, clr
endmodule

module _16registre (
  input  [15:0] I,
  input  in_2,
  input  [1:0] s_e,
  output [15:0] out_4,
  output [15:0] O
);

  Register #(.width(16)) register_1 (.D(I), .Q(out_4), .clk(s_e[1]), .clr(in_2));  // open: en
  assign O = s_e[0] ? out_4 : 16'bz;  // Controlled_Buffer controlled_buffer_1
  Pull_Resistor pull_resistor_1 (.node(s_e[0]));
endmodule
